// Logisim project LAB.circ as structural Verilog: 5 circuits, main circuit CONTROL
module CONTROL (
  input  CLK_1,
  input  LED_1,
  input  PLAYER_1,
  input  LED_8,
  input  RESET,
  input  LED_2,
  input  LED_3,
  input  LED_4,
  input  LED_5,
  input  LED_6,
  input  LED_7,
  output RESET_RIGHT,
  output S0,
  output RESET_LEFT,
  output S1,
  output R2,
  output R3,
  output R4,
  output R5,
  output R6,
  output R7
);

  wire and_1_out, and_2_out, and_4_out, d_ff_1_qn, d_ff_2_qn, not_1_out, or_1_out, or_2_out, or_3_out;

  and and_1 (and_1_out, LED_1, PLAYER_1);
  and and_2 (and_2_out, PLAYER_1, LED_8);
  or or_1 (or_1_out, and_1_out, and_2_out);
  or or_2 (or_2_out, LED_2, LED_3, LED_4, LED_5, LED_6, LED_7);
  and and_3 (R2, PLAYER_1, or_2_out);
  D_Flip_Flop d_ff_1 (.D(d_ff_1_qn), .clk(or_1_out), .Q(S0), .Qn(d_ff_1_qn), .reset(and_4_out));  // open: preset
  and and_4 (and_4_out, or_3_out, LED_8);
  or or_3 (or_3_out, or_1_out, RESET, R2);
  not not_1 (not_1_out, PLAYER_1);
  D_Flip_Flop d_ff_2 (.D(d_ff_2_qn), .clk(or_3_out), .Q(S1), .Qn(d_ff_2_qn), .reset(and_4_out));  // open: preset
  and and_5 (RESET_RIGHT, not_1_out, CLK_1, LED_1);
  and and_6 (RESET_LEFT, not_1_out, CLK_1, LED_8, S0, S1);

  assign R3 = R2;
  assign R4 = R2;
  assign R5 = R2;
  assign R6 = R2;
  assign R7 = R2;
endmodule

module CORE (
  input  R2,
  input  R3,
  input  R4,
  input  R5,
  input  R6,
  input  R7,
  input  RESET_LEFT,
  input  RESET_RIGHT,
  input  CLK1,
  input  S0,
  input  S1,
  output LED_1,
  output LED_2,
  output LED_3,
  output LED_4,
  output LED_5,
  output LED_6,
  output LED_7,
  output LED_8
);

  wire mux_four_to_one_1_f, mux_four_to_one_2_f, mux_four_to_one_3_f, mux_four_to_one_4_f,
       mux_four_to_one_5_f, mux_four_to_one_6_f, mux_four_to_one_7_f, mux_four_to_one_8_f;

  MUX_FOUR_TO_ONE mux_four_to_one_1 (
    .S0(S0), .S1(S1), .I0(LED_2), .I1(1'b0), .I2(1'b0), .I3(LED_8), .F(mux_four_to_one_1_f));
  D_Flip_Flop d_ff_1 (.D(mux_four_to_one_1_f), .clk(CLK1), .Q(LED_1), .reset(RESET_LEFT));  // open: Qn, preset
  MUX_FOUR_TO_ONE mux_four_to_one_2 (
    .S0(S0), .S1(S1), .I0(LED_3), .I1(1'b0), .I2(1'b0), .I3(LED_1), .F(mux_four_to_one_2_f));
  D_Flip_Flop d_ff_2 (.D(mux_four_to_one_2_f), .clk(CLK1), .Q(LED_2), .reset(R2));  // open: Qn, preset
  MUX_FOUR_TO_ONE mux_four_to_one_3 (
    .S0(S0), .S1(S1), .I0(LED_4), .I1(1'b0), .I2(1'b0), .I3(LED_2), .F(mux_four_to_one_3_f));
  D_Flip_Flop d_ff_3 (.D(mux_four_to_one_3_f), .clk(CLK1), .Q(LED_3), .reset(R3));  // open: Qn, preset
  MUX_FOUR_TO_ONE mux_four_to_one_4 (
    .S0(S0), .S1(S1), .I0(LED_5), .I1(1'b0), .I2(1'b0), .I3(LED_3), .F(mux_four_to_one_4_f));
  D_Flip_Flop d_ff_4 (.D(mux_four_to_one_4_f), .clk(CLK1), .Q(LED_4), .reset(R4));  // open: Qn, preset
  MUX_FOUR_TO_ONE mux_four_to_one_5 (
    .S0(S0), .S1(S1), .I0(LED_6), .I1(1'b0), .I2(1'b0), .I3(LED_4), .F(mux_four_to_one_5_f));
  D_Flip_Flop d_ff_5 (.D(mux_four_to_one_5_f), .clk(CLK1), .Q(LED_5), .reset(R5));  // open: Qn, preset
  MUX_FOUR_TO_ONE mux_four_to_one_6 (
    .S0(S0), .S1(S1), .I0(LED_7), .I1(1'b0), .I2(1'b0), .I3(LED_5), .F(mux_four_to_one_6_f));
  D_Flip_Flop d_ff_6 (.D(mux_four_to_one_6_f), .clk(CLK1), .Q(LED_6), .reset(R6));  // open: Qn, preset
  D_Flip_Flop d_ff_7 (.D(mux_four_to_one_7_f), .clk(CLK1), .Q(LED_7), .reset(R7));  // open: Qn, preset
  MUX_FOUR_TO_ONE mux_four_to_one_7 (
    .S0(S0), .S1(S1), .I0(LED_8), .I1(1'b0), .I2(1'b0), .I3(LED_6), .F(mux_four_to_one_7_f));
  D_Flip_Flop d_ff_8 (.D(mux_four_to_one_8_f), .clk(CLK1), .Q(LED_8), .reset(RESET_RIGHT));  // open: Qn, preset
  MUX_FOUR_TO_ONE mux_four_to_one_8 (
    .S0(S0), .S1(S1), .I0(LED_1), .I1(1'b1), .I2(1'b1), .I3(LED_7), .F(mux_four_to_one_8_f));
endmodule

module MUX_FOUR_TO_ONE (
  input  S0,
  input  S1,
  input  I0,
  input  I1,
  input  I2,
  input  I3,
  output F
);

  wire and_1_out, and_2_out, and_3_out, and_4_out, not_1_out, not_2_out;

  not not_1 (not_1_out, S0);
  not not_2 (not_2_out, S1);
  and and_1 (and_1_out, I0, not_1_out, not_2_out);
  and and_2 (and_2_out, I1, S0, not_2_out);
  and and_3 (and_3_out, I2, not_1_out, S1);
  and and_4 (and_4_out, I3, S0, S1);
  or or_1 (F, and_1_out, and_2_out, and_3_out, and_4_out);
endmodule

module FINAL_MAIN (
);

  wire CLK_out, control_1_r2, control_1_r3, control_1_r4, control_1_r5, control_1_r6, control_1_r7,
       control_1_reset_left, control_1_reset_right, control_1_s0, control_1_s1, core_1_led_1, core_1_led_2,
       core_1_led_3, core_1_led_4, core_1_led_5, core_1_led_6, core_1_led_7, core_1_led_8, PLAYER_1_out,
       RESET_out;

  Clock CLK (.out(CLK_out));
  Button PLAYER_1 (.out(PLAYER_1_out));
  Button RESET (.out(RESET_out));
  CONTROL control_1 (
    .CLK_1(CLK_out), .LED_1(core_1_led_1), .PLAYER_1(PLAYER_1_out), .LED_8(core_1_led_8), .RESET(RESET_out),
    .LED_2(core_1_led_2), .LED_3(core_1_led_3), .LED_4(core_1_led_4), .LED_5(core_1_led_5),
    .LED_6(core_1_led_6), .LED_7(core_1_led_7), .RESET_RIGHT(control_1_reset_right), .S0(control_1_s0),
    .RESET_LEFT(control_1_reset_left), .S1(control_1_s1), .R2(control_1_r2), .R3(control_1_r3),
    .R4(control_1_r4), .R5(control_1_r5), .R6(control_1_r6), .R7(control_1_r7));
  CORE core_1 (
    .R2(control_1_r2), .R3(control_1_r3), .R4(control_1_r4), .R5(control_1_r5), .R6(control_1_r6),
    .R7(control_1_r7), .RESET_LEFT(control_1_reset_left), .RESET_RIGHT(control_1_reset_right),
    .CLK1(CLK_out), .S0(control_1_s0), .S1(control_1_s1), .LED_1(core_1_led_1), .LED_2(core_1_led_2),
    .LED_3(core_1_led_3), .LED_4(core_1_led_4), .LED_5(core_1_led_5), .LED_6(core_1_led_6),
    .LED_7(core_1_led_7), .LED_8(core_1_led_8));
  EXTRA extra_1 (.PLAYER_1(PLAYER_1_out), .LED_1(core_1_led_1), .LED_8(core_1_led_8));
  LED led_1 (.in(core_1_led_1));
  LED led_2 (.in(core_1_led_2));
  LED led_3 (.in(core_1_led_3));
  LED led_4 (.in(core_1_led_4));
  LED led_5 (.in(core_1_led_5));
  LED led_6 (.in(core_1_led_6));
  LED led_7 (.in(core_1_led_7));
  LED led_8 (.in(core_1_led_8));
endmodule

module EXTRA (
  input  PLAYER_1,
  input  LED_1,
  input  LED_8
);

  wire and_1_out, and_2_out, or_1_out;

  and and_1 (and_1_out, PLAYER_1, LED_1);
  and and_2 (and_2_out, PLAYER_1, LED_8);
  or or_1 (or_1_out, and_1_out, and_2_out);
  // Buzzer #(.vol_width(1)) buzzer_1: pin names not known; wires that end beside it: 14'h1f4, or_1_out, 1'b1
endmodule
